// Logisim project Q4.1_UniversalGates.circ as structural Verilog: 1 circuit, main circuit main
module main (
  input  X,
  input  Y,
  input  Z,
  input  W,
  output F
);

  wire nand_1_out, nand_2_out, nand_3_out;

  nand nand_1 (nand_1_out, X, Y);
  nand nand_2 (nand_2_out, nand_1_out, Z);
  nand nand_3 (nand_3_out, nand_1_out, W);
  nand nand_4 (F, nand_2_out, nand_3_out);

  // Notes on the sheet:
  //   Question 4.1 Universal Gates
  //   Therefore, 4 NAND gates are needed
  //   Output
endmodule
