// Logisim project Q4.2_ParityCounter.circ as structural Verilog: 1 circuit, main circuit main
module main (
  input  A,
  input  B,
  input  C,
  input  D,
  output F0,
  output F1,
  output F2
);

  wire F0_0_out, F0_1_out, F0_2_out, F0_3_out, F0_4_out, F0_5_out, F0_6_out, F0_7_out, F1_0_out, F1_1_out,
       F1_2_out, F1_3_out, F1_4_out, F1_5_out, F1_6_out, F1_7_out, F1_8_out, F1_9_out, not_1_out, not_2_out,
       not_3_out, not_4_out;

  not not_1 (not_1_out, A);
  not not_2 (not_2_out, B);
  not not_3 (not_3_out, C);
  not not_4 (not_4_out, D);
  and F0_0 (F0_0_out, not_1_out, not_2_out, not_3_out, D);
  and F0_1 (F0_1_out, not_1_out, not_2_out, C, not_4_out);
  and F0_2 (F0_2_out, not_1_out, B, not_3_out, not_4_out);
  and F0_3 (F0_3_out, not_1_out, B, C, D);
  and F0_4 (F0_4_out, A, not_2_out, not_3_out, not_4_out);
  and F0_5 (F0_5_out, A, not_2_out, C, D);
  and F0_6 (F0_6_out, A, B, not_3_out, D);
  and F0_7 (F0_7_out, A, B, C, not_4_out);
  and F1_0 (F1_0_out, not_1_out, not_2_out, C, D);
  and F1_1 (F1_1_out, not_1_out, B, not_3_out, D);
  and F1_2 (F1_2_out, not_1_out, B, C, not_4_out);
  and F1_3 (F1_3_out, not_1_out, B, C, D);
  and F1_4 (F1_4_out, A, not_2_out, not_3_out, D);
  and F1_5 (F1_5_out, A, not_2_out, C, not_4_out);
  and F1_6 (F1_6_out, A, not_2_out, C, D);
  and F1_7 (F1_7_out, A, B, not_3_out, not_4_out);
  and F1_8 (F1_8_out, A, B, not_3_out, D);
  and F1_9 (F1_9_out, A, B, C, not_4_out);
  and F2_0 (F2, A, B, C, D);
  or u_F0 (F0, F0_0_out, F0_1_out, F0_2_out, F0_3_out, F0_4_out, F0_5_out, F0_6_out, F0_7_out);
  or u_F1 (F1, F1_0_out, F1_1_out, F1_2_out, F1_3_out, F1_4_out, F1_5_out, F1_6_out, F1_7_out, F1_8_out, F1_9_out);
endmodule
