// Logisim project Q4.3_FullAddersAndHalfAdders.circ as structural Verilog: 1 circuit, main circuit main
module main (
  input  A6,
  input  A5,
  input  A4,
  input  A3,
  input  A2,
  input  A1,
  input  A0,
  output out_8,
  output Output,
  output out_10
);

  wire adder_1_cout, adder_1_out, adder_2_cout, adder_2_out, adder_4_cout;

  Adder #(.width(1)) adder_1 (.a(A6), .b(A5), .out(adder_1_out), .cin(A4), .cout(adder_1_cout));
  Adder #(.width(1)) adder_2 (.a(A3), .b(A2), .out(adder_2_out), .cin(A1), .cout(adder_2_cout));
  Adder #(.width(1)) adder_3 (.a(adder_1_cout), .b(adder_2_cout), .out(Output), .cin(adder_4_cout), .cout(out_8));
  Adder #(.width(1)) adder_4 (.a(adder_1_out), .b(adder_2_out), .out(out_10), .cin(A0), .cout(adder_4_cout));

  // Notes on the sheet:
  //   Question 4.3
  //   4 full-adders are needed
  //   Input
  //   Most significant bit
  //   Then add up those two numbers, and take the last bit as carry-in
  //   First, use two full-adders to generate two 2-bit numbers -> responsible for the first 6 digits
  //   Least significant bit
endmodule
