// Logisim project shift.circ as structural Verilog: 1 circuit, main circuit main
module main (
  input  [1:0] in_1,
  input  B_in,
  output B_out,
  output A7,
  output A6
);

  Clock clock_1 ();  // open: out
  Multiplexer #(.select(2), .enable("false")) multiplexer_1 (.sel(in_1));  // open: in0, in1, in2, in3, out
  D_Flip_Flop d_ff_1 ();  // open: clk, D, Q, Qn, preset, reset
  D_Flip_Flop d_ff_2 ();  // open: clk, D, Q, Qn, preset, reset
endmodule
